# Fritzing sketch HitagiExpansionBoard (saved by Fritzing 0.9.5d)
breadboards: 1

parts:
  BRIGHTNESS = TRIMPOT [package=trimpot-3mm]
  SparkFun_Pro_Micro_5v = SparkFun Pro Micro [part_number=DEV-12640]
  STEMMA = female pin header, 4 pins [form="♀ (female)"]
  RESET = Pushbutton [package="[THT]"]
  BAT1 = BC9VPC [package=bc9vpc]
  POWER = Toggle Switch [package=THT]
  23LC1024 = 23LCV1024 [part_number=23LC1024 package="DIP (Dual Inline) [THT]"]
  STEMMA1 = Adafruit Stemma 4 pin header [form="♀ (female)" package=THT]
  STEMMA2 = Adafruit Stemma 4 pin header [form="♀ (female)" package=THT]
  R7 = Resistor [tolerance=±5% resistance=10k package="0805 [SMD]"]
  R5 = Resistor [tolerance=±5% resistance=10k package="0805 [SMD]"]
  R6 = Resistor [tolerance=±5% resistance=10k package="0805 [SMD]"]
  STEMMA3 = Adafruit Stemma 4 pin header [form="♀ (female)" package=THT]
  PWM(5) = female pin header, 3 pins [form="♀ (female)"]
  SPI0 = JST PH SPI HEADER [form="♀ (female)" package=THT]
  SPI1 = JST PH SPI HEADER [form="♀ (female)" package=THT]
  SPI2 = JST PH SPI HEADER [form="♀ (female)" package=THT]
  D7 = female pin header, 3 pins [form="♀ (female)"]
  C2 = Ceramic Capacitor [capacitance=0.1µF voltage=50V package="0805 [SMD, multilayer]"]
  SPI3 = JST PH SPI HEADER [form="♀ (female)" package=THT]
  Part1 = TFT 2.2 inch 320x240 w microSD [part_number=1480]
  SPI_Selector = IC, DIP package, 16 pins [chip_label=74HC138 part_number=74HC138]
  C3 = Ceramic Capacitor [capacitance=100nF voltage=50V package="0805 [SMD, multilayer]"]
  23LC1025 = 23LCV1024 [part_number=23LC1024 package="DIP (Dual Inline) [THT]"]
  R8 = Resistor [tolerance=±5% resistance=10k package="0805 [SMD]"]
  R9 = Resistor [tolerance=±5% resistance=10k package="0805 [SMD]"]
  R10 = Resistor [tolerance=±5% resistance=10k package="0805 [SMD]"]

nets:
  23LC1024 GND/GND/SELECT GND: BRIGHTNESS.CCW, SparkFun_Pro_Micro_5v.GND, STEMMA.pin1, RESET.Pin_3, RESET.Pin_4, BAT1.V-, 23LC1024.VSS, STEMMA1.GND, STEMMA2.GND, STEMMA3.GND, PWM(5).pin1, SPI0.GND, SPI1.GND, SPI2.GND, D7.pin1, C2.0, SPI3.GND, Part1.GND, SPI_Selector.pin5, SPI_Selector.pin8, C3.0
  CONTRAST: BRIGHTNESS.WIPER, Part1.BACKLIGHT
  23LC1024 VCC/5V/SELECT VCC: BRIGHTNESS.CW, SparkFun_Pro_Micro_5v.VCC, STEMMA.pin2, 23LC1024.VCC, STEMMA1.V+, STEMMA2.V+, R7.Pin_0, R5.Pin_0, R6.Pin_0, STEMMA3.V+, PWM(5).pin2, SPI0.VCC, SPI1.VCC, SPI2.VCC, D7.pin2, C2.1, SPI3.VCC, Part1.VIN, SPI_Selector.pin6, SPI_Selector.pin16, C3.1, R8.Pin_0, R9.Pin_0, R10.Pin_0
  9V: SparkFun_Pro_Micro_5v.RAW, POWER.COM
  RESET: SparkFun_Pro_Micro_5v.RESET, RESET.Pin_1
  SCK: SparkFun_Pro_Micro_5v.SCK, 23LC1024.SCK, SPI0.SCK, SPI1.SCK, SPI2.SCK, SPI3.SCK, Part1.SCLK, 23LC1025.SCK
  MISO: SparkFun_Pro_Micro_5v.MISO, 23LC1024.SO/SIO1, SPI0.MISO, SPI1.MISO, SPI2.MISO, SPI3.MISO, Part1.MISO, 23LC1025.SO/SIO1
  MOSI: SparkFun_Pro_Micro_5v.MOSI, 23LC1024.SI/SIO0, SPI0.MOSI, SPI1.MOSI, SPI2.MOSI, SPI3.MOSI, Part1.MOSI, 23LC1025.SI/SIO0
  D7: SparkFun_Pro_Micro_5v.D7, D7.pin3
  PWM0: SparkFun_Pro_Micro_5v.D5, PWM(5).pin3
  SCL: SparkFun_Pro_Micro_5v.D3, STEMMA.pin4, STEMMA1.SCL, STEMMA2.SCL, STEMMA3.SCL
  SDA: SparkFun_Pro_Micro_5v.D2, STEMMA.pin3, STEMMA1.SDA, STEMMA2.SDA, STEMMA3.SDA
  9V IN: BAT1.V+, POWER.L1
  SRAM Enable: 23LC1024.CS_, R7.Pin_1, SPI_Selector.pin15
  N1: 23LC1024.NC, R5.Pin_1
  N2: 23LC1024.VBAT, R6.Pin_1
  SPI0 Enable: SPI0.CS_, SPI_Selector.pin11
  SPI1 Enable: SPI1.CS_, SPI_Selector.pin10
  SPI2 Enable: SPI2.CS_, SPI_Selector.pin9
  SPI3 Enable: SPI3.CS_, SPI_Selector.pin7
  SDCS: Part1.SDCS, SPI_Selector.pin12
  LCD Enable: Part1.LCDCS, SPI_Selector.pin13
  SEL0: SPI_Selector.pin1
  SEL1: SPI_Selector.pin2
  SEL2: SPI_Selector.pin3
  SEL3: SPI_Selector.pin4
  SRAM2 Enable: SPI_Selector.pin14, 23LC1025.CS_, R9.Pin_1
  N3: 23LC1025.NC, R8.Pin_1
  23LC10242 GND: 23LC1025.VSS
  N4: 23LC1025.VBAT, R10.Pin_1
  23LC10242 VCC: 23LC1025.VCC

notes:
  REV 2
  "Hitagi" Expansion Board
  (C) 2020 Joshua Scoggins

custom parts:
  SparkFun Pro Micro: This tiny little board does all of the neat-o Arduino tricks that you’re familiar with: 4 channels of 10-bit ADC, 5 PWM pins, 12 DIOs as well as hardware serial connections Rx and Tx. Running at 16MHz and 5V, this board will remind you a lot of your other favorite Arduino-compatible boards but this little guy can go just about anywhere. There is a voltage regulator on board so it can accept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
  Adafruit Stemma 4 pin header: Adafruit STEMMA 4 pin header JST PH 4
  JST PH SPI HEADER: Single device JST PH Based SPI Header
  TFT 2.2 inch 320x240 w microSD: This lovely little display breakout is the best way to add a small, colorful and bright display to any project. Since the display uses 4-wire SPI to communicate and has its own pixel-addressable frame buffer, it can be used with every kind of microcontroller. Even a very small one with low memory and few pins available! The 2.2" display has 320x240 color pixels.
